// Logisim project ControlTruth.circ as structural Verilog: 1 circuit, main circuit ControlTruth
module ControlTruth (
  input  [1:0] OpCode,
  output RegDst,
  output ALU,
  output MemtoReg,
  output RegWrite,
  output MemWrite,
  output [1:0] ALUOp
);

  wire not_1_out;

  or or_1 (RegDst, OpCode[0], OpCode[1]);
  not not_1 (not_1_out, OpCode[0]);
  and and_1 (MemWrite, OpCode[0], OpCode[1]);
  or or_2 (ALU, not_1_out, OpCode[1]);

  assign ALUOp = 2'b00;
  assign MemtoReg = OpCode[1];
  assign RegWrite = 1'b1;
endmodule
